# Fritzing sketch RouchBT (saved by Fritzing 0.4.3b)
breadboards: 1

parts:
  IC1 = H-Bridge [package=THT]
  Arduino1 = Arduino
  M1 = DC Motor
  M2 = DC Motor
  VCC1 = Battery block 9V
  U1 = mystery part, 4 pins [chip_label="BlueSmirf Gold" spacing=300mil]

nets:
  N1: IC1.1_2EN, Arduino1.D11
  N2: IC1.1A, Arduino1.D13
  N3: IC1.1Y, M2.pin_1
  GND1: IC1.GND1, IC1.GND2, IC1.GND3, IC1.GND4, Arduino1.GND, VCC1.-
  N4: IC1.2Y, M2.pin_2
  N5: IC1.2A, Arduino1.D12
  N6: IC1.VCC2, Arduino1.VIN, VCC1.+
  N7: IC1.3_4EN, Arduino1.D6
  N8: IC1.3A, Arduino1.D7
  N9: IC1.3Y, M1.pin_2
  N10: IC1.4Y, M1.pin_1
  N11: IC1.4A, Arduino1.D8
  N12: IC1.VCC1, Arduino1.+5V
  N13: Arduino1.D1TX, U1.pin4
  N14: Arduino1.D0RX, U1.pin3
